# Fritzing sketch PCB_header (saved by Fritzing 0.9.10b)
circuit board: 6.48338cm x 5.86376cm
breadboards: 1

parts:
  MCP3008 = MCP3008 [package=dil16]
  R1 = Resistor [tolerance=±5% resistance=1M power=0.25 package=THT]
  R2 = Resistor [tolerance=±5% resistance=1M power=0.25 package=THT]
  R3 = Resistor [tolerance=±5% resistance=1M power=0.25 package=THT]
  R4 = Resistor [tolerance=±5% resistance=1M power=0.25 package=THT]
  R5 = Resistor [tolerance=±5% power=0.25 resistance=220 package=THT]
  R6 = Resistor [tolerance=±5% power=0.25 resistance=220 package=THT]
  R7 = Resistor [tolerance=±5% power=0.25 resistance=220 package=THT]
  Humidity = male pin header, 3 pins [form="♂ (male)"]
  Moisture = male pin header, 5 pins [form="♂ (male)"]
  LED1 = RGB LED - (4 legs) [package="5 mm [THT]"]
  water_level = male pin header, 3 pins [form="♂ (male)"]
  R8 = Resistor [tolerance=±5% power=0.25 resistance=10k package=THT]
  Shutdown = male pin header, 2 pins [form="♂ (male)"]
  Raspberry_Pi_1 = Raspberry Pi 3 [part_number=RPI-3-V1.2]

nets:
  N1: MCP3008.CH0, R1.Pin_1, Moisture.pin2
  N2: MCP3008.CH1, R2.Pin_1, Moisture.pin3
  N3: MCP3008.CH2, R3.Pin_1, Moisture.pin4
  N4: MCP3008.CH3, R4.Pin_1, water_level.pin3
  N5: MCP3008.DGND, MCP3008.AGND, R1.Pin_0, R2.Pin_0, R3.Pin_0, R4.Pin_0, Humidity.pin1, Moisture.pin5, water_level.pin1, Raspberry_Pi_1.GND
  N6: MCP3008.CS/SHDN, Raspberry_Pi_1.GIPO8
  N7: MCP3008.Din, Raspberry_Pi_1.GIPO10
  N8: MCP3008.Dout, Raspberry_Pi_1.GIPO9
  N9: MCP3008.CLK, Raspberry_Pi_1.GIPO11
  3V3: MCP3008.VREF, MCP3008.VDD, Humidity.pin2, Moisture.pin1, LED1.common_anode, water_level.pin2, Shutdown.pin2, Raspberry_Pi_1.3v3, Raspberry_Pi_1.3V3
  N10: R5.Pin_0, LED1.blue_cathode
  N11: R5.Pin_1, Raspberry_Pi_1.GIPO26
  N12: R6.Pin_0, LED1.green_cathode
  N13: R6.Pin_1, Raspberry_Pi_1.GIPO19
  N14: R7.Pin_0, LED1.red_cathode
  N15: R7.Pin_1, Raspberry_Pi_1.GIPO13
  N16: Humidity.pin3, Raspberry_Pi_1.GIPO4
  N17: R8.Pin_0, Shutdown.pin1
  N18: R8.Pin_1, Raspberry_Pi_1.GIPO6

notes:
  +
  -
